# Fritzing sketch schema_electrique (saved by Fritzing 0.9.2b)
breadboards: 1

parts:
  Composant1 = Arduino Uno (Rev3)  # not connected
  M1 = Stepper Motor - Unipolar  # not connected
  M2 = Stepper Motor - Unipolar  # not connected
  R1 = PHOTOCELL [package=photocell]
  R2 = PHOTOCELL [package=photocell]
  R3 = PHOTOCELL [package=photocell]
  R4 = PHOTOCELL [package=photocell]
  R5 = Resistor [tolerance=±5% resistance=220 package="0402 [SMD]"]
  R6 = Resistor [tolerance=±5% resistance=220 package="0402 [SMD]"]
  R7 = Resistor [tolerance=±5% resistance=220 package="0402 [SMD]"]
  R8 = Resistor [tolerance=±5% resistance=220 package="0402 [SMD]"]

nets:
  N1: R1.P$1, R6.Pin_1
  N2: R2.P$2, R5.Pin_0
  N3: R3.P$1, R7.Pin_1
  N4: R4.P$2, R8.Pin_0
  N5: R5.Pin_1, R8.Pin_1
  N6: R6.Pin_0, R7.Pin_0
